// Logisim project ALU.circ as structural Verilog
module ALU (
  input  [31:0] in_1,
  input  [31:0] in_2,
  input  [2:0] in_3,
  output [31:0] OP
);

  wire [0:0] SLT, SLTU;
  wire [31:0] ADD, AND, not_1_out, OR, SUB, XOR;

  Adder #(.width(32)) adder_1 (.a(in_1), .b(in_2), .out(ADD));  // open: cin, cout
  Subtractor #(.width(32)) subtractor_1 (.a(in_1), .b(in_2), .out(SUB));  // open: bin, bout
  assign AND = in_1 & in_2;  // AND_Gate and_1, 32 bits wide
  assign OR = in_1 | in_2;  // OR_Gate or_1, 32 bits wide
  assign not_1_out = ~OR;  // NOT_Gate not_1, 32 bits wide
  assign XOR = in_1 ^ in_2;  // XOR_Gate xor_1, 32 bits wide
  Multiplexer #(.select(3), .width(32), .enable("false")) multiplexer_1 (
    .in0(ADD), .in1(SUB), .in2(AND), .in3(OR), .in4(not_1_out), .in5(XOR), .in6({{31{1'b0}}, SLT[0]}),
    .in7({{31{1'b0}}, SLTU[0]}), .out(OP), .sel(in_3));
  Comparator #(.width(32)) comparator_1 (.a(in_1), .b(in_2), .lt(SLT[0]));  // open: gt, eq
  Comparator #(.width(32), .mode("unsigned")) comparator_2 (.a(in_1), .b(in_2), .lt(SLTU[0]));  // open: gt, eq

  // Other names for the same wires on the sheet: OP_SELECT[2:0] = in_3; RS[31:0] = in_1; RT[31:0] = in_2

  // Notes on the sheet:
  //   Inputs
  //   Arithmetic
  //   ADD
  //   SUB
  //   AND
  //   Logic
  //   OR
  //   Operations
  //   XOR
  //   Outputs
  //   SLT
  //   Comparison
  //   SLTU
endmodule

module Two_s_Complement (
  input  [31:0] in_1,
  output [31:0] out_2
);

  wire [31:0] not_1_out;

  assign not_1_out = ~in_1;  // NOT_Gate not_1, 32 bits wide
  Adder #(.width(32)) adder_1 (.a(not_1_out), .b(32'h1), .out(out_2));  // open: cin, cout
endmodule

module Absolute_Value (
  input  [31:0] in_1,
  output [31:0] out_2
);

  wire [31:0] two_s_complement_1_out_2;

  Two_s_Complement two_s_complement_1 (.out_2(two_s_complement_1_out_2), .in_1(in_1));
  Multiplexer #(.width(32), .enable("false")) multiplexer_1 (
    .in0(in_1), .in1(two_s_complement_1_out_2), .out(out_2), .sel(in_1[31]));
endmodule

module Register_File (
  input  [4:0] in_1,
  input  [4:0] in_2,
  input  [4:0] in_3,
  input  [31:0] in_4,
  input  in_5,
  input  in_6,
  output [31:0] RS,
  output [31:0] RT
);

  wire W0, W1, W2, W3, W4, W5, W6, W7, W8, W9, W10, W11, W12, W13, W14, W15, W16, W17, W18, W19, W20, W21,
       W22, W23, W24, W25, W26, W27, W28, W29, W30, W31;
  wire [31:0] R0, R1, R2, R3, R4, R5, R6, R7, R8, R9, R10, R11, R12, R13, R14, R15, R16, R17, R18, R19, R20,
       R21, R22, R23, R24, R25, R26, R27, R28, R29, R30, R31;

  Register #(.width(32)) u_R0 (.D({32{1'b0}}), .en(W0), .Q(R0), .clk(in_6));  // open: clr
  Register #(.width(32)) u_R8 (.D(in_4), .en(W8), .Q(R8), .clk(in_6));  // open: clr
  Register #(.width(32)) u_R16 (.D(in_4), .en(W16), .Q(R16), .clk(in_6));  // open: clr
  Register #(.width(32)) u_R24 (.D(in_4), .en(W24), .Q(R24), .clk(in_6));  // open: clr
  Decoder #(.select(5)) decoder_1 (
    .out0(W0), .out1(W1), .out2(W2), .out3(W3), .out4(W4), .out5(W5), .out6(W6), .out7(W7), .out8(W8),
    .out9(W9), .out10(W10), .out11(W11), .out12(W12), .out13(W13), .out14(W14), .out15(W15), .out16(W16),
    .out17(W17), .out18(W18), .out19(W19), .out20(W20), .out21(W21), .out22(W22), .out23(W23), .out24(W24),
    .out25(W25), .out26(W26), .out27(W27), .out28(W28), .out29(W29), .out30(W30), .out31(W31), .sel(in_3),
    .en(in_5));
  Register #(.width(32)) u_R1 (.D(in_4), .en(W1), .Q(R1), .clk(in_6));  // open: clr
  Register #(.width(32)) u_R9 (.D(in_4), .en(W9), .Q(R9), .clk(in_6));  // open: clr
  Register #(.width(32)) u_R17 (.D(in_4), .en(W17), .Q(R17), .clk(in_6));  // open: clr
  Register #(.width(32)) u_R25 (.D(in_4), .en(W25), .Q(R25), .clk(in_6));  // open: clr
  Register #(.width(32)) u_R2 (.D(in_4), .en(W2), .Q(R2), .clk(in_6));  // open: clr
  Register #(.width(32)) u_R10 (.D(in_4), .en(W10), .Q(R10), .clk(in_6));  // open: clr
  Register #(.width(32)) u_R18 (.D(in_4), .en(W18), .Q(R18), .clk(in_6));  // open: clr
  Register #(.width(32)) u_R26 (.D(in_4), .en(W26), .Q(R26), .clk(in_6));  // open: clr
  Register #(.width(32)) u_R3 (.D(in_4), .en(W3), .Q(R3), .clk(in_6));  // open: clr
  Register #(.width(32)) u_R11 (.D(in_4), .en(W11), .Q(R11), .clk(in_6));  // open: clr
  Register #(.width(32)) u_R19 (.D(in_4), .en(W19), .Q(R19), .clk(in_6));  // open: clr
  Register #(.width(32)) u_R27 (.D(in_4), .en(W27), .Q(R27), .clk(in_6));  // open: clr
  Multiplexer #(.select(5), .width(32), .enable("false")) multiplexer_1 (
    .in0(R0), .in1(R1), .in2(R2), .in3(R3), .in4(R4), .in5(R5), .in6(R6), .in7(R7), .in8(R8), .in9(R9),
    .in10(R10), .in11(R11), .in12(R12), .in13(R13), .in14(R14), .in15(R15), .in16(R16), .in17(R17),
    .in18(R18), .in19(R19), .in20(R20), .in21(R21), .in22(R22), .in23(R23), .in24(R24), .in25(R25),
    .in26(R26), .in27(R27), .in28(R28), .in29(R29), .in30(R30), .in31(R31), .out(RS), .sel(in_1));
  Register #(.width(32)) u_R4 (.D(in_4), .en(W4), .Q(R4), .clk(in_6));  // open: clr
  Register #(.width(32)) u_R12 (.D(in_4), .en(W12), .Q(R12), .clk(in_6));  // open: clr
  Register #(.width(32)) u_R20 (.D(in_4), .en(W20), .Q(R20), .clk(in_6));  // open: clr
  Register #(.width(32)) u_R28 (.D(in_4), .en(W28), .Q(R28), .clk(in_6));  // open: clr
  Register #(.width(32)) u_R5 (.D(in_4), .en(W5), .Q(R5), .clk(in_6));  // open: clr
  Register #(.width(32)) u_R13 (.D(in_4), .en(W13), .Q(R13), .clk(in_6));  // open: clr
  Register #(.width(32)) u_R21 (.D(in_4), .en(W21), .Q(R21), .clk(in_6));  // open: clr
  Register #(.width(32)) u_R29 (.D(in_4), .en(W29), .Q(R29), .clk(in_6));  // open: clr
  Register #(.width(32)) u_R6 (.D(in_4), .en(W6), .Q(R6), .clk(in_6));  // open: clr
  Register #(.width(32)) u_R14 (.D(in_4), .en(W14), .Q(R14), .clk(in_6));  // open: clr
  Register #(.width(32)) u_R22 (.D(in_4), .en(W22), .Q(R6), .clk(in_6));  // open: clr
  Register #(.width(32)) u_R30 (.D(in_4), .en(W30), .Q(R30), .clk(in_6));  // open: clr
  Multiplexer #(.select(5), .width(32), .enable("false")) multiplexer_2 (
    .in0(R0), .in1(R1), .in2(R2), .in3(R3), .in4(R4), .in5(R5), .in6(R6), .in7(R7), .in8(R8), .in9(R9),
    .in10(R10), .in11(R11), .in12(R12), .in13(R13), .in14(R14), .in15(R15), .in16(R16), .in17(R17),
    .in18(R18), .in19(R19), .in20(R20), .in21(R21), .in22(R22), .in23(R23), .in24(R24), .in25(R25),
    .in26(R26), .in27(R27), .in28(R28), .in29(R29), .in30(R30), .in31(R31), .out(RT), .sel(in_2));
  Register #(.width(32)) u_R7 (.D(in_4), .en(W7), .Q(R7), .clk(in_6));  // open: clr
  Register #(.width(32)) u_R15 (.D(in_4), .en(W15), .Q(R15), .clk(in_6));  // open: clr
  Register #(.width(32)) u_R23 (.D(in_4), .en(W23), .Q(R23), .clk(in_6));  // open: clr
  Register #(.width(32)) SP (.D(in_4), .en(W31), .Q(R31), .clk(in_6));  // open: clr

  // Other names for the same wires on the sheet: CLOCK = in_6; RS_ID[4:0] = in_1; RT_ID[4:0] = in_2; W = in_5;
  //   W_DATA[31:0] = in_4; W_ID[4:0] = in_3

  // Notes on the sheet:
  //   Inputs
  //   WRITE
  //   Registers
  //   Outputs
endmodule

module HILO_Register (
  input  [31:0] in_1,
  input  [31:0] in_2,
  input  in_3,
  input  in_4,
  output [31:0] HI,
  output [31:0] LO
);

  Register #(.width(32)) u_HI (.D(in_1), .en(in_3), .Q(HI), .clk(in_4));  // open: clr
  Register #(.width(32)) u_LO (.D(in_2), .en(in_3), .Q(LO), .clk(in_4));  // open: clr

  // Other names for the same wires on the sheet: CLOCK = in_4; W = in_3; W_HI[31:0] = in_1; W_LO[31:0] = in_2

  // Notes on the sheet:
  //   Inputs
  //   Outputs
endmodule

module Immediate_Extender (
  input  [15:0] in_1,
  input  in_2,
  output [31:0] out_3
);

  wire [15:0] bit_extender_1_out;

  assign bit_extender_1_out = {{15{in_1[15]}}, in_1[15]};  // Bit_Extender bit_extender_1
  Multiplexer #(.width(16), .enable("false")) multiplexer_1 (
    .in0(bit_extender_1_out), .in1({16{1'b0}}), .out(out_3[31:16]), .sel(in_2));

  assign out_3[15:0] = in_1;

  // Other names for the same wires on the sheet: CONST[15:0] = in_1; SELECT = in_2

  // Notes on the sheet:
  //   Inputs
  //   Outputs
endmodule

module Datapath (
  input  [31:0] in_1
);

  wire ALU_W, CLOCK, CONST_OP, CONST_W, MULTDIV_W;
  wire [1:0] MULTDIV_OP;
  wire [2:0] ALU_OP;
  wire [4:0] RD_ID, RS_ID, RT_ID;
  wire [5:0] instruction_decoder_1_func_code, instruction_decoder_1_op_code;
  wire [15:0] CONST;
  wire [31:0] ALU_OUTPUT, immediate_extender_1_out_3, multdiv_unit_1_hi, multdiv_unit_1_lo,
       multiplexer_1_out, multiplexer_2_out, PC_PLUS_4, PC_q, RS, RT;

  Clock clock_1 (.out(CLOCK));
  Instruction_Decoder instruction_decoder_1 (
    .in_1(in_1), .FUNC_CODE(instruction_decoder_1_func_code), .OP_CODE(instruction_decoder_1_op_code),
    .RS(RS_ID), .RT(RT_ID), .RD(RD_ID), .CONST(CONST));  // open: JUMP
  Register_File register_file_1 (
    .in_1(RS_ID), .in_2(RT_ID), .in_3(RD_ID), .in_4(ALU_OUTPUT), .in_5(ALU_W), .in_6(CLOCK), .RS(RS), .RT(RT));
  ALU_Control alu_control_1 (
    .in_1(instruction_decoder_1_op_code), .in_2(instruction_decoder_1_func_code), .ALU_OP(ALU_OP),
    .MULTDIV_OP(MULTDIV_OP), .ALU_W(ALU_W), .MULTDIV_W(MULTDIV_W), .CONST_OP(CONST_OP), .CONST_W(CONST_W));
  Immediate_Extender immediate_extender_1 (.in_1(CONST), .in_2(CONST_OP), .out_3(immediate_extender_1_out_3));
  MultDiv_Unit multdiv_unit_1 (.in_1(RS), .in_2(RT), .in_3(MULTDIV_OP), .HI(multdiv_unit_1_hi), .LO(multdiv_unit_1_lo));
  Multiplexer #(.select(2), .width(32), .enable("false")) multiplexer_1 (
    .in0(PC_PLUS_4), .out(multiplexer_1_out));  // open: in1, in2, in3, sel
  Multiplexer #(.width(32), .enable("false")) multiplexer_2 (
    .in0(RT), .in1(immediate_extender_1_out_3), .out(multiplexer_2_out), .sel(CONST_W));
  Register #(.width(32)) PC (.D(multiplexer_1_out), .Q(PC_q), .clk(CLOCK));  // open: en, clr
  ALU alu_1 (.OP(ALU_OUTPUT), .in_2(multiplexer_2_out), .in_1(RS), .in_3(ALU_OP));
  HILO_Register hilo_register_1 (
    .in_1(multdiv_unit_1_hi), .in_2(multdiv_unit_1_lo), .in_4(CLOCK), .in_3(MULTDIV_W));  // open: HI, LO
  Adder #(.width(32)) adder_1 (.a(PC_q), .b(32'h4), .out(PC_PLUS_4));  // open: cin, cout

  // Other names for the same wires on the sheet: INSTRUCTION[31:0] = in_1
endmodule

module ALU_Control (
  input  [5:0] in_1,
  input  [5:0] in_2,
  output ALU_W,
  output [2:0] ALU_OP,
  output MULTDIV_W,
  output [1:0] MULTDIV_OP,
  output CONST_W,
  output CONST_OP
);

  wire ADD, ADD_out, ADDI, AND, AND_3_out, ANDI, comparator_1_eq, comparator_4_eq, comparator_7_eq,
       comparator_10_eq, comparator_12_eq, comparator_13_eq, comparator_14_eq, comparator_15_eq,
       comparator_16_eq, comparator_17_eq, comparator_18_eq, comparator_19_eq, DIV, DIVU, MULT, MULU, NOR,
       OR, or_2_out, or_3_out, OR_out, ORI, priority_encoder_1_en_out, priority_encoder_2_en_out,
       priority_encoder_3_en_out, priority_encoder_3_out, R_TYPE, SLT, SLT_out, SLTI, SLTIU, SLTU, SLTU_out,
       SUB, XOR, XOR_out, XORI;
  wire [1:0] priority_encoder_2_out;
  wire [2:0] priority_encoder_1_out;

  Comparator #(.width(6), .mode("unsigned")) comparator_1 (
    .a(6'b100000), .b(in_2), .eq(comparator_1_eq));  // open: gt, lt
  Comparator #(.width(6), .mode("unsigned")) comparator_2 (.a(6'b001000), .b(in_1), .eq(ADDI));  // open: gt, lt
  Comparator #(.width(6), .mode("unsigned")) comparator_3 (.a(6'b001101), .b(in_1), .eq(ORI));  // open: gt, lt
  Comparator #(.width(6), .mode("unsigned")) comparator_4 (
    .a(6'b101010), .b(in_2), .eq(comparator_4_eq));  // open: gt, lt
  Comparator #(.width(6), .mode("unsigned")) comparator_5 (.a(6'b001010), .b(in_1), .eq(SLTI));  // open: gt, lt
  and and_1 (ADD, R_TYPE, comparator_1_eq);
  and and_2 (SLT, R_TYPE, comparator_4_eq);
  Comparator #(.width(6)) comparator_6 (.a(in_1), .b({6{1'b0}}), .eq(R_TYPE));  // open: gt, lt
  or u_ADD (ADD_out, ADD, ADDI);
  or AND_3 (AND_3_out, AND, ANDI);
  or u_OR (OR_out, OR, ORI);
  or u_XOR (XOR_out, XOR, XORI);
  or u_SLT (SLT_out, SLT, SLTI);
  or u_SLTU (SLTU_out, SLTU, SLTIU);
  Comparator #(.width(6), .mode("unsigned")) comparator_7 (
    .a(6'b100010), .b(in_2), .eq(comparator_7_eq));  // open: gt, lt
  Comparator #(.width(6), .mode("unsigned")) comparator_8 (.a(6'b001100), .b(in_1), .eq(ANDI));  // open: gt, lt
  Comparator #(.width(6), .mode("unsigned")) comparator_9 (.a(6'b001110), .b(in_1), .eq(XORI));  // open: gt, lt
  Comparator #(.width(6), .mode("unsigned")) comparator_10 (
    .a(6'b101011), .b(in_2), .eq(comparator_10_eq));  // open: gt, lt
  Comparator #(.width(6), .mode("unsigned")) comparator_11 (.a(6'b001011), .b(in_1), .eq(SLTIU));  // open: gt, lt
  and and_4 (SLTU, R_TYPE, comparator_10_eq);
  and and_5 (SUB, R_TYPE, comparator_7_eq);
  not not_1 (ALU_W, priority_encoder_1_en_out);
  Priority_Encoder priority_encoder_1 (
    .in0(ADD_out), .in1(SUB), .in2(AND_3_out), .in3(OR_out), .in4(NOR), .in5(XOR_out), .in6(SLT_out),
    .in7(SLTU_out), .out(priority_encoder_1_out), .en_out(priority_encoder_1_en_out));  // open: en_in, gs
  Multiplexer #(.width(3), .enable("false")) multiplexer_1 (
    .in0(priority_encoder_1_out), .in1(3'b000), .out(ALU_OP), .sel(priority_encoder_1_en_out));
  Comparator #(.width(6), .mode("unsigned")) comparator_12 (
    .a(6'b011000), .b(in_2), .eq(comparator_12_eq));  // open: gt, lt
  Comparator #(.width(6), .mode("unsigned")) comparator_13 (
    .a(6'b011001), .b(in_2), .eq(comparator_13_eq));  // open: gt, lt
  Comparator #(.width(6), .mode("unsigned")) comparator_14 (
    .a(6'b100100), .b(in_2), .eq(comparator_14_eq));  // open: gt, lt
  Comparator #(.width(6), .mode("unsigned")) comparator_15 (
    .a(6'b100111), .b(in_2), .eq(comparator_15_eq));  // open: gt, lt
  and and_6 (MULT, R_TYPE, comparator_12_eq);
  and and_7 (MULU, R_TYPE, comparator_13_eq);
  and and_8 (AND, R_TYPE, comparator_14_eq);
  and and_9 (NOR, R_TYPE, comparator_15_eq);
  not not_2 (MULTDIV_W, priority_encoder_2_en_out);
  Priority_Encoder #(.select(2)) priority_encoder_2 (
    .in0(MULT), .in1(MULU), .in2(DIV), .in3(DIVU), .out(priority_encoder_2_out),
    .en_out(priority_encoder_2_en_out));  // open: gs, en_in
  Multiplexer #(.width(2), .enable("false")) multiplexer_2 (
    .in0(priority_encoder_2_out), .in1(2'b00), .out(MULTDIV_OP), .sel(priority_encoder_2_en_out));
  Comparator #(.width(6), .mode("unsigned")) comparator_16 (
    .a(6'b011010), .b(in_2), .eq(comparator_16_eq));  // open: gt, lt
  Comparator #(.width(6), .mode("unsigned")) comparator_17 (
    .a(6'b011011), .b(in_2), .eq(comparator_17_eq));  // open: gt, lt
  Comparator #(.width(6), .mode("unsigned")) comparator_18 (
    .a(6'b100101), .b(in_2), .eq(comparator_18_eq));  // open: gt, lt
  Comparator #(.width(6), .mode("unsigned")) comparator_19 (
    .a(6'b101000), .b(in_2), .eq(comparator_19_eq));  // open: gt, lt
  and and_10 (DIV, R_TYPE, comparator_16_eq);
  and and_11 (DIVU, R_TYPE, comparator_17_eq);
  and and_12 (OR, R_TYPE, comparator_18_eq);
  and and_13 (XOR, R_TYPE, comparator_19_eq);
  or or_2 (or_2_out, ADDI, SLTI, SLTIU);
  or or_3 (or_3_out, ANDI, ORI, XORI);
  not not_3 (CONST_W, priority_encoder_3_en_out);
  Priority_Encoder #(.select(1)) priority_encoder_3 (
    .in0(or_2_out), .in1(or_3_out), .out(priority_encoder_3_out), .en_out(priority_encoder_3_en_out));  // open: gs, en_in
  Multiplexer #(.enable("false")) multiplexer_3 (
    .in0(priority_encoder_3_out), .in1(1'b0), .out(CONST_OP), .sel(priority_encoder_3_en_out));

  // Other names for the same wires on the sheet: FUNC_CODE[5:0] = in_2; OP_CODE[5:0] = in_1

  // Notes on the sheet:
  //   Inputs
  //   ADD
  //   ADDI
  //   ORI
  //   SLT
  //   SLTI
  //   SLTU
  //   SLTIU
  //   SUB
  //   ANDI
  //   XORI
  //   MULT
  //   MULU
  //   AND
  //   NOR
  //   DIV
  //   DIVU
  //   OR
  //   XOR
endmodule

module MultDiv_Unit (
  input  [31:0] in_1,
  input  [31:0] in_2,
  input  [1:0] in_3,
  output [31:0] HI,
  output [31:0] LO
);

  wire [31:0] DIV_HI, DIV_LO, DIVU_HI, DIVU_LO, MULT_HI, MULT_LO, MULU_HI, MULU_LO;

  Mult mult_1 (.in_1(in_1), .in_2(in_2), .LO(MULT_LO), .HI(MULT_HI));
  Multiplier #(.width(32)) multiplier_1 (.a(in_1), .b(in_2), .out(MULU_LO), .cout(MULU_HI));  // open: cin
  Multiplexer #(.select(2), .width(32), .enable("false")) multiplexer_1 (
    .in0(MULT_LO), .in1(MULU_LO), .in2(DIV_LO), .in3(DIVU_LO), .out(LO), .sel(in_3));
  Div div_1 (.in_1(in_1), .in_2(in_2), .LO(DIV_LO), .HI(DIV_HI));
  Multiplexer #(.select(2), .width(32), .enable("false")) multiplexer_2 (
    .in0(MULT_HI), .in1(MULU_HI), .in2(DIV_HI), .in3(DIVU_HI), .out(HI), .sel(in_3));
  Divider #(.width(32)) divider_1 (.a(in_1), .b(in_2), .out(DIVU_LO), .rem(DIVU_HI));  // open: upper

  // Other names for the same wires on the sheet: OP_SELECT[1:0] = in_3; RS[31:0] = in_1; RT[31:0] = in_2

  // Notes on the sheet:
  //   Inputs
  //   MULT
  //   MULU
  //   Operations
  //   DIV
  //   Outputs
  //   DIVU
endmodule

module Mult (
  input  [31:0] in_1,
  input  [31:0] in_2,
  output [31:0] LO,
  output [31:0] HI
);

  wire adder_1_cout, SIGN;
  wire [31:0] absolute_value_1_out_2, absolute_value_2_out_2, adder_1_out, adder_2_out, bit_extender_1_out,
       multiplier_1_cout, multiplier_1_out, not_1_out, not_2_out;

  xor xor_1 (SIGN, in_1[31], in_2[31]);
  Absolute_Value absolute_value_1 (.in_1(in_1), .out_2(absolute_value_1_out_2));
  Absolute_Value absolute_value_2 (.in_1(in_2), .out_2(absolute_value_2_out_2));
  Multiplier #(.width(32)) multiplier_1 (
    .a(absolute_value_1_out_2), .b(absolute_value_2_out_2), .out(multiplier_1_out), .cout(multiplier_1_cout));  // open: cin
  assign not_1_out = ~multiplier_1_out;  // NOT_Gate not_1, 32 bits wide
  assign not_2_out = ~multiplier_1_cout;  // NOT_Gate not_2, 32 bits wide
  Adder #(.width(32)) adder_1 (.a(not_1_out), .b(32'h1), .out(adder_1_out), .cout(adder_1_cout));  // open: cin
  assign bit_extender_1_out = {{31{1'b0}}, adder_1_cout};  // Bit_Extender bit_extender_1
  Adder #(.width(32)) adder_2 (.a(bit_extender_1_out), .b(not_2_out), .out(adder_2_out));  // open: cin, cout
  Multiplexer #(.width(32), .enable("false")) multiplexer_1 (
    .in0(multiplier_1_out), .in1(adder_1_out), .out(LO), .sel(SIGN));
  Multiplexer #(.width(32), .enable("false")) multiplexer_2 (
    .in0(multiplier_1_cout), .in1(adder_2_out), .out(HI), .sel(SIGN));

  // Other names for the same wires on the sheet: RS[31:0] = in_1; RT[31:0] = in_2
endmodule

module Div (
  input  [31:0] in_1,
  input  [31:0] in_2,
  output [31:0] LO,
  output [31:0] HI
);

  wire SIGN;
  wire [31:0] absolute_value_1_out_2, absolute_value_2_out_2, divider_1_out, divider_1_rem,
       two_s_complement_1_out_2, two_s_complement_2_out_2;

  xor xor_1 (SIGN, in_1[31], in_2[31]);
  Absolute_Value absolute_value_1 (.in_1(in_1), .out_2(absolute_value_1_out_2));
  Absolute_Value absolute_value_2 (.in_1(in_2), .out_2(absolute_value_2_out_2));
  Divider #(.width(32)) divider_1 (
    .a(absolute_value_1_out_2), .b(absolute_value_2_out_2), .out(divider_1_out), .rem(divider_1_rem));  // open: upper
  Two_s_Complement two_s_complement_1 (.out_2(two_s_complement_1_out_2), .in_1(divider_1_out));
  Two_s_Complement two_s_complement_2 (.out_2(two_s_complement_2_out_2), .in_1(divider_1_rem));
  Multiplexer #(.width(32), .enable("false")) multiplexer_1 (
    .in0(divider_1_out), .in1(two_s_complement_1_out_2), .out(LO), .sel(SIGN));
  Multiplexer #(.width(32), .enable("false")) multiplexer_2 (
    .in0(divider_1_rem), .in1(two_s_complement_2_out_2), .out(HI), .sel(in_1[31]));

  // Other names for the same wires on the sheet: RS[31:0] = in_1; RT[31:0] = in_2
endmodule

module Instruction_Decoder (
  input  [31:0] in_1,
  output [5:0] OP_CODE,
  output [4:0] RS,
  output [4:0] RT,
  output [4:0] RD,
  output [5:0] FUNC_CODE,
  output [25:0] JUMP,
  output [15:0] CONST
);


  assign CONST = in_1[15:0];
  assign FUNC_CODE = in_1[5:0];
  assign JUMP = in_1[25:0];
  assign OP_CODE = in_1[31:26];
  assign RD = in_1[15:11];
  assign RS = in_1[25:21];
  assign RT = in_1[20:16];

  // Other names for the same wires on the sheet: Instruction[31:0] = in_1
endmodule
