// Logisim project Control Unit.circ as structural Verilog: 3 circuits, main circuit main
module main (
  input  [31:0] Instruction,
  input  [1:0] Flags,
  input  [3:0] R_time,
  input  [3:0] W_time,
  input  RESET,
  input  Clock,
  output [3:0] Alu_op,
  output Const_op,
  output [4:0] Rs,
  output [4:0] Rt,
  output Const_enab,
  output Register_File_write,
  output [4:0] Register_write,
  output [2:0] Register_select,
  output [1:0] Branch_op,
  output [15:0] Const,
  output Hi_Lo_Register_write,
  output Sp_op,
  output [1:0] Ram_address_select,
  output [25:0] Jump,
  output Ram_value_select,
  output CS,
  output RAM_R_W,
  output LOAD_SP,
  output LOAD_PC,
  output STOP,
  output TTY_ENABLE,
  output KBD_ENABLE
);

  wire comparator_1_lt, CS_0, CS_1, CS_2, CS_3, CS_4, d_ff_1_q, d_ff_3_q, d_ff_8_q, d_ff_9_q, d_ff_13_q,
       demultiplexer_1_out0, demultiplexer_1_out1, demultiplexer_2_out0, demultiplexer_3_out2,
       demultiplexer_3_out3, demultiplexer_3_out4, demultiplexer_3_out5, demultiplexer_4_out0,
       demultiplexer_4_out1, demultiplexer_5_out0, demultiplexer_6_out0, demultiplexer_7_out0,
       demultiplexer_7_out1, demultiplexer_8_out0, demultiplexer_8_out1, demultiplexer_9_out0,
       demultiplexer_9_out1, demultiplexer_10_out0, demultiplexer_10_out1, HI_LO_W, LOAD_INST, LOAD_SP_0,
       LOAD_SP_1, not_1_out, not_2_out, not_3_out, not_4_out, not_5_out, not_6_out, or_5_out, or_6_out,
       or_7_out, or_8_out, or_9_out, or_10_out, RAM_OP, REG_W, REG_W_0, REG_W_1, REG_W_2, REG_W_4, REG_W_5,
       STACK_OP, WAIT;
  wire [1:0] SPECIAL_OP;
  wire [2:0] OP;
  wire [3:0] counter_1_q, WAIT_T;
  wire [4:0] instruction_decoder_1_rd;
  wire [5:0] instruction_decoder_1_func_code, instruction_decoder_1_op_code;
  wire [31:0] register_1_q;

  Multiplexer #(.width(4), .enable("false")) multiplexer_1 (.in0(R_time), .in1(W_time), .out(WAIT_T), .sel(RAM_R_W));
  Counter #(.width(4), .max('hf)) counter_1 (
    .count(CS), .Q(counter_1_q), .clk(Clock), .clr(or_5_out));  // open: load, D, carry
  or or_1 (CS, CS_0, CS_1, CS_2, CS_3, CS_4);
  or or_2 (REG_W, REG_W_0, REG_W_1, REG_W_2, LOAD_SP_0, REG_W_4, REG_W_5);
  or or_3 (RAM_R_W, CS_2, CS_4);
  or or_4 (LOAD_SP, LOAD_SP_0, LOAD_SP_1);
  D_Flip_Flop d_ff_1 (.clk(Clock), .D(demultiplexer_1_out0), .Q(d_ff_1_q), .preset(RESET));  // open: Qn, en, reset
  Demultiplexer #(.enable("false")) demultiplexer_1 (
    .out0(demultiplexer_1_out0), .out1(demultiplexer_1_out1), .in(d_ff_1_q), .sel(not_1_out));
  not not_1 (not_1_out, RESET);
  Comparator #(.width(4), .mode("unsigned")) comparator_1 (
    .a(WAIT_T), .b(counter_1_q), .gt(WAIT), .lt(comparator_1_lt));  // open: eq
  or or_5 (or_5_out, comparator_1_lt, RESET);
  or or_6 (or_6_out, demultiplexer_2_out0, d_ff_13_q, demultiplexer_1_out1);
  Register #(.width(32)) register_1 (.D(Instruction), .en(LOAD_INST), .Q(register_1_q), .clk(Clock), .clr(RESET));
  D_Flip_Flop d_ff_2 (.clk(Clock), .D(or_6_out), .Q(CS_0), .reset(RESET));  // open: Qn, preset, en
  Demultiplexer #(.enable("false")) demultiplexer_2 (
    .out0(demultiplexer_2_out0), .out1(LOAD_INST), .in(CS_0), .sel(not_2_out));
  not not_2 (not_2_out, WAIT);
  Instruction_Decoder instruction_decoder_1 (
    .Instruction(register_1_q), .FUNC_CODE(instruction_decoder_1_func_code),
    .OP_CODE(instruction_decoder_1_op_code), .RS(Rs), .RT(Rt), .RD(instruction_decoder_1_rd), .JUMP(Jump),
    .CONST(Const));
  // Probe on instruction_decoder_1_op_code
  D_Flip_Flop d_ff_3 (.clk(Clock), .D(LOAD_INST), .Q(d_ff_3_q), .reset(RESET));  // open: Qn, preset, en
  // Probe on instruction_decoder_1_func_code
  Demultiplexer #(.select(3), .enable("false")) demultiplexer_3 (
    .out0(REG_W_0), .out1(REG_W_1), .out2(demultiplexer_3_out2), .out3(demultiplexer_3_out3),
    .out4(demultiplexer_3_out4), .out5(demultiplexer_3_out5), .in(d_ff_3_q), .sel(OP));  // open: out6, out7
  Operation_Decoder operation_decoder_1 (
    .Rt(Rt), .Rd(instruction_decoder_1_rd), .Op_code(instruction_decoder_1_op_code),
    .Func_code(instruction_decoder_1_func_code), .Flags(Flags), .Write_address(Register_write),
    .HI_LO_write(HI_LO_W), .Alu_op(Alu_op), .Const_enable(Const_enab), .Const_op(Const_op),
    .Branch_op(Branch_op), .Register_Select(Register_select), .Sp_op(Sp_op), .Op(OP), .Ram_op(RAM_OP),
    .Stack_op(STACK_OP), .Special_op(SPECIAL_OP), .Ram_address_select(Ram_address_select),
    .Ram_value_select(Ram_value_select));
  Demultiplexer #(.enable("false")) demultiplexer_4 (
    .out0(demultiplexer_4_out0), .out1(demultiplexer_4_out1), .in(demultiplexer_3_out3), .sel(RAM_OP));
  Demultiplexer #(.enable("false")) demultiplexer_5 (
    .out0(demultiplexer_5_out0), .out1(LOAD_SP_1), .in(demultiplexer_3_out4), .sel(STACK_OP));
  Demultiplexer #(.select(2), .enable("false")) demultiplexer_6 (
    .out0(demultiplexer_6_out0), .out1(TTY_ENABLE), .out2(REG_W_4), .out3(REG_W_5),
    .in(demultiplexer_3_out5), .sel(SPECIAL_OP));
  or or_7 (or_7_out, demultiplexer_7_out0, demultiplexer_4_out0);
  or or_8 (or_8_out, demultiplexer_8_out0, demultiplexer_4_out1);
  or or_9 (or_9_out, demultiplexer_9_out0, demultiplexer_5_out0);
  or or_10 (or_10_out, demultiplexer_10_out0, LOAD_SP_1);
  or or_11 (STOP, d_ff_8_q, demultiplexer_6_out0);
  and and_1 (Register_File_write, REG_W, ~HI_LO_W);  // AND_Gate
  and and_2 (Hi_Lo_Register_write, REG_W, HI_LO_W);
  D_Flip_Flop d_ff_4 (.clk(Clock), .D(or_7_out), .Q(CS_1), .reset(RESET));  // open: Qn, preset, en
  D_Flip_Flop d_ff_5 (.clk(Clock), .D(or_8_out), .Q(CS_2), .reset(RESET));  // open: Qn, preset, en
  D_Flip_Flop d_ff_6 (.clk(Clock), .D(or_9_out), .Q(CS_3), .reset(RESET));  // open: Qn, preset, en
  D_Flip_Flop d_ff_7 (.clk(Clock), .D(or_10_out), .Q(CS_4), .reset(RESET));  // open: Qn, preset, en
  D_Flip_Flop d_ff_8 (.clk(Clock), .D(STOP), .Q(d_ff_8_q), .reset(RESET));  // open: Qn, preset, en
  D_Flip_Flop d_ff_9 (.clk(Clock), .D(TTY_ENABLE), .Q(d_ff_9_q), .reset(RESET));  // open: Qn, preset, en
  D_Flip_Flop d_ff_10 (.clk(Clock), .D(REG_W_5), .Q(KBD_ENABLE), .reset(RESET));  // open: Qn, preset, en
  Demultiplexer #(.enable("false")) demultiplexer_7 (
    .out0(demultiplexer_7_out0), .out1(demultiplexer_7_out1), .in(CS_1), .sel(not_4_out));
  Demultiplexer #(.enable("false")) demultiplexer_8 (
    .out0(demultiplexer_8_out0), .out1(demultiplexer_8_out1), .in(CS_2), .sel(not_3_out));
  not not_3 (not_3_out, WAIT);
  Demultiplexer #(.enable("false")) demultiplexer_9 (
    .out0(demultiplexer_9_out0), .out1(demultiplexer_9_out1), .in(CS_3), .sel(not_5_out));
  Demultiplexer #(.enable("false")) demultiplexer_10 (
    .out0(demultiplexer_10_out0), .out1(demultiplexer_10_out1), .in(CS_4), .sel(not_6_out));
  not not_4 (not_4_out, WAIT);
  not not_5 (not_5_out, WAIT);
  not not_6 (not_6_out, WAIT);
  D_Flip_Flop d_ff_11 (.clk(Clock), .D(demultiplexer_7_out1), .Q(REG_W_2), .reset(RESET));  // open: Qn, preset, en
  D_Flip_Flop d_ff_12 (.clk(Clock), .D(demultiplexer_9_out1), .Q(LOAD_SP_0), .reset(RESET));  // open: Qn, preset, en
  or or_12 (LOAD_PC, REG_W_0, REG_W_1, demultiplexer_3_out2, REG_W_2, demultiplexer_8_out1, LOAD_SP_0, demultiplexer_10_out1, d_ff_9_q, REG_W_4, KBD_ENABLE);
  D_Flip_Flop d_ff_13 (.clk(Clock), .D(LOAD_PC), .Q(d_ff_13_q), .reset(RESET));  // open: Qn, preset, en

  // Other names for the same wires on the sheet: INST[31:0] = Instruction; RAM_W = RAM_R_W; RAM_W_0 = CS_2;
  //   RAM_W_1 = CS_4; REG_W_3 = LOAD_SP_0; WAIT_INIT = CS

  // Notes on the sheet:
  //   ALU
  //   Register
  //   Branch
  //   Ram
  //   Stack
  //   Special
  //   rnd
  //   kbd
  //   Read
  //   Write
  //   Pop
  //   Push
  //   Halt
  //   tty
endmodule

module Instruction_Decoder (
  input  [31:0] Instruction,
  output [5:0] OP_CODE,
  output [4:0] RS,
  output [4:0] RT,
  output [4:0] RD,
  output [5:0] FUNC_CODE,
  output [25:0] JUMP,
  output [15:0] CONST
);


  assign CONST = Instruction[15:0];
  assign FUNC_CODE = Instruction[5:0];
  assign JUMP = Instruction[25:0];
  assign OP_CODE = Instruction[31:26];
  assign RD = Instruction[15:11];
  assign RS = Instruction[25:21];
  assign RT = Instruction[20:16];

  // Other names for the same wires on the sheet: INST[31:0] = Instruction
endmodule

module Operation_Decoder (
  input  [4:0] Rt,
  input  [4:0] Rd,
  input  [5:0] Op_code,
  input  [5:0] Func_code,
  input  [1:0] Flags,
  output Const_enable,
  output Const_op,
  output [4:0] Write_address,
  output Ram_value_select,
  output [3:0] Alu_op,
  output [1:0] Ram_address_select,
  output [2:0] Op,
  output Sp_op,
  output Stack_op,
  output HI_LO_write,
  output Ram_op,
  output [1:0] Branch_op,
  output [2:0] Register_Select,
  output [1:0] Special_op
);

  wire _000000, _111000, _111111, ADD, ADD_out, ADDI, ALU, AND, and_5_out, AND_9_out, and_16_out, and_17_out,
       and_18_out, and_19_out, and_20_out, and_21_out, and_22_out, ANDI, BEQ, BGTZ, BLEZ, BLTZ, BNE, BRANCH,
       comparator_4_eq, comparator_5_eq, comparator_6_eq, comparator_9_eq, comparator_10_eq,
       comparator_11_eq, comparator_12_eq, comparator_15_eq, comparator_16_eq, comparator_19_eq,
       comparator_20_eq, comparator_23_eq, comparator_24_eq, comparator_26_eq, comparator_27_eq,
       comparator_29_eq, comparator_31_eq, comparator_32_eq, comparator_34_eq, comparator_37_eq,
       comparator_38_eq, comparator_39_eq, DIV, DIVU, HALT, J, JR, KBD, LW, MFHI, MFLO, MULT, MULU, NOP, NOR,
       OR, or_1_out, or_2_out, OR_3_out, or_4_out, or_5_out, or_6_out, or_7_out, or_9_out, or_10_out,
       or_11_out, ORI, POP, priority_encoder_1_en_out, priority_encoder_1_out, priority_encoder_2_en_out,
       priority_encoder_4_en_out, priority_encoder_5_en_out, priority_encoder_5_out,
       priority_encoder_6_en_out, priority_encoder_7_en_out, priority_encoder_8_en_out,
       priority_encoder_8_out, priority_encoder_9_en_out, RAM, RND, SLT, SLT_out, SLTI, SLTIU, SLTU,
       SLTU_out, SPECIAL, STACK, SUB, SUB_out, SW, TTY, XOR, XOR_out, XORI;
  wire [1:0] priority_encoder_2_out, priority_encoder_6_out, priority_encoder_9_out;
  wire [2:0] priority_encoder_7_out;
  wire [3:0] priority_encoder_4_out;

  Comparator #(.width(6)) comparator_1 (.a(Op_code), .b({6{1'b0}}), .eq(_000000));  // open: gt, lt
  Comparator #(.width(6)) comparator_2 (.a(Op_code), .b(6'b111000), .eq(_111000));  // open: gt, lt
  Comparator #(.width(6)) comparator_3 (.a(Op_code), .b({6{1'b1}}), .eq(_111111));  // open: gt, lt
  Comparator #(.width(6), .mode("unsigned")) comparator_4 (
    .a(6'b100000), .b(Func_code), .eq(comparator_4_eq));  // open: gt, lt
  Comparator #(.width(6), .mode("unsigned")) comparator_5 (
    .a(6'b100100), .b(Func_code), .eq(comparator_5_eq));  // open: gt, lt
  Comparator #(.width(6), .mode("unsigned")) comparator_6 (
    .a(6'b101010), .b(Func_code), .eq(comparator_6_eq));  // open: gt, lt
  Comparator #(.width(6), .mode("unsigned")) comparator_7 (.a(6'b000100), .b(Op_code), .eq(BEQ));  // open: gt, lt
  Comparator #(.width(6), .mode("unsigned")) comparator_8 (.a(6'b100011), .b(Op_code), .eq(LW));  // open: gt, lt
  Comparator #(.width(6), .mode("unsigned")) comparator_9 (
    .a(6'b000100), .b(Func_code), .eq(comparator_9_eq));  // open: gt, lt
  and and_1 (SLT, _000000, comparator_6_eq);
  and and_2 (ADD, _000000, comparator_4_eq);
  and and_3 (AND, _000000, comparator_5_eq);
  and and_4 (KBD, _111111, comparator_9_eq);
  not not_1 (RAM, priority_encoder_1_en_out);
  Priority_Encoder #(.select(1)) priority_encoder_1 (
    .in0(LW), .in1(SW), .out(priority_encoder_1_out), .en_out(priority_encoder_1_en_out));  // open: gs, en_in
  not not_2 (SPECIAL, priority_encoder_2_en_out);
  and and_5 (and_5_out, ALU, ~BEQ, ~BNE);  // AND_Gate
  or or_1 (or_1_out, MFHI, MFLO);
  or or_2 (or_2_out, NOP, BRANCH);
  Multiplexer #(.enable("false")) multiplexer_1 (
    .in0(priority_encoder_1_out), .in1(1'b0), .out(Ram_op), .sel(priority_encoder_1_en_out));
  Priority_Encoder #(.select(2)) priority_encoder_2 (
    .in0(HALT), .in1(TTY), .in2(RND), .in3(KBD), .out(priority_encoder_2_out),
    .en_out(priority_encoder_2_en_out));  // open: gs, en_in
  Multiplexer #(.width(2), .enable("false")) multiplexer_2 (
    .in0(priority_encoder_2_out), .in1(2'b00), .out(Special_op), .sel(priority_encoder_2_en_out));
  Comparator #(.width(6), .mode("unsigned")) comparator_10 (
    .a(6'b100010), .b(Func_code), .eq(comparator_10_eq));  // open: gt, lt
  Comparator #(.width(6), .mode("unsigned")) comparator_11 (
    .a(6'b100101), .b(Func_code), .eq(comparator_11_eq));  // open: gt, lt
  Comparator #(.width(6), .mode("unsigned")) comparator_12 (
    .a(6'b101011), .b(Func_code), .eq(comparator_12_eq));  // open: gt, lt
  Comparator #(.width(6), .mode("unsigned")) comparator_13 (.a(6'b000101), .b(Op_code), .eq(BNE));  // open: gt, lt
  Comparator #(.width(6), .mode("unsigned")) comparator_14 (.a(6'b101011), .b(Op_code), .eq(SW));  // open: gt, lt
  and and_6 (SUB, _000000, comparator_10_eq);
  and and_7 (OR, _000000, comparator_11_eq);
  and and_8 (SLTU, _000000, comparator_12_eq);
  Priority_Encoder priority_encoder_3 (
    .in0(and_5_out), .in1(or_1_out), .in2(or_2_out), .in3(RAM), .in4(STACK), .in5(SPECIAL), .out(Op));  // open: in6, in7, en_in, gs, en_out
  Comparator #(.width(6), .mode("unsigned")) comparator_15 (
    .a(6'b011000), .b(Func_code), .eq(comparator_15_eq));  // open: gt, lt
  Comparator #(.width(6), .mode("unsigned")) comparator_16 (
    .a(6'b100111), .b(Func_code), .eq(comparator_16_eq));  // open: gt, lt
  Comparator #(.width(6), .mode("unsigned")) comparator_17 (.a(6'b001010), .b(Op_code), .eq(SLTI));  // open: gt, lt
  Comparator #(.width(6), .mode("unsigned")) comparator_18 (.a(6'b000110), .b(Op_code), .eq(BLEZ));  // open: gt, lt
  Comparator #(.width(6), .mode("unsigned")) comparator_19 (
    .a({6{1'b0}}), .b(Func_code), .eq(comparator_19_eq));  // open: gt, lt
  or u_ADD (ADD_out, ADD, ADDI);
  or u_SUB (SUB_out, SUB, BEQ, BNE);
  or AND_9 (AND_9_out, AND, ANDI);
  or OR_3 (OR_3_out, OR, ORI);
  or u_XOR (XOR_out, XOR, XORI);
  or u_SLT (SLT_out, SLT, SLTI);
  or u_SLTU (SLTU_out, SLTU, SLTIU);
  and and_10 (MULT, _000000, comparator_15_eq);
  and and_11 (NOR, _000000, comparator_16_eq);
  and and_12 (POP, _111000, comparator_19_eq);
  not not_3 (ALU, priority_encoder_4_en_out);
  Multiplexer #(.width(4), .enable("false")) multiplexer_3 (
    .in0(priority_encoder_4_out), .in1(4'b0000), .out(Alu_op), .sel(priority_encoder_4_en_out));
  Priority_Encoder #(.select(4)) priority_encoder_4 (
    .in0(ADD_out), .in1(SUB_out), .in2(AND_9_out), .in3(OR_3_out), .in4(NOR), .in5(XOR_out), .in6(SLT_out),
    .in7(SLTU_out), .in8(MULT), .in9(MULU), .in10(DIV), .in11(DIVU), .out(priority_encoder_4_out),
    .en_out(priority_encoder_4_en_out));  // open: in12, in13, in14, in15, gs, en_in
  Comparator #(.width(6), .mode("unsigned")) comparator_20 (
    .a(6'b011001), .b(Func_code), .eq(comparator_20_eq));  // open: gt, lt
  Comparator #(.width(6), .mode("unsigned")) comparator_21 (.a(6'b001011), .b(Op_code), .eq(SLTIU));  // open: gt, lt
  Comparator #(.width(6), .mode("unsigned")) comparator_22 (.a(6'b000111), .b(Op_code), .eq(BGTZ));  // open: gt, lt
  Comparator #(.width(6), .mode("unsigned")) comparator_23 (
    .a(6'b101000), .b(Func_code), .eq(comparator_23_eq));  // open: gt, lt
  Comparator #(.width(6), .mode("unsigned")) comparator_24 (
    .a(6'b000001), .b(Func_code), .eq(comparator_24_eq));  // open: gt, lt
  and and_13 (MULU, _000000, comparator_20_eq);
  and and_14 (XOR, _000000, comparator_23_eq);
  and and_15 (Ram_value_select, _111000, comparator_24_eq);
  or or_4 (or_4_out, Flags[1], Flags[0]);
  and and_16 (and_16_out, ~Flags[1], ~Flags[0]);  // AND_Gate
  and and_17 (and_17_out, Flags[1], ~Flags[0]);  // AND_Gate
  and and_18 (and_18_out, BEQ, Flags[0]);
  and and_19 (and_19_out, BNE, ~Flags[0]);  // AND_Gate
  and and_20 (and_20_out, BLEZ, or_4_out);
  and and_21 (and_21_out, BGTZ, and_16_out);
  and and_22 (and_22_out, BLTZ, and_17_out);
  or or_5 (or_5_out, ADDI, SLTI, SLTIU, LW, SW);
  or or_6 (or_6_out, ANDI, ORI, XORI);
  Comparator #(.width(6), .mode("unsigned")) comparator_25 (.a(6'b001100), .b(Op_code), .eq(ANDI));  // open: gt, lt
  or or_7 (or_7_out, and_18_out, and_19_out, and_20_out, and_21_out, and_22_out);
  Comparator #(.width(6), .mode("unsigned")) comparator_26 (
    .a(6'b011010), .b(Func_code), .eq(comparator_26_eq));  // open: gt, lt
  Comparator #(.width(6), .mode("unsigned")) comparator_27 (
    .a(6'b010000), .b(Func_code), .eq(comparator_27_eq));  // open: gt, lt
  Comparator #(.width(6), .mode("unsigned")) comparator_28 (.a(6'b000001), .b(Op_code), .eq(BLTZ));  // open: gt, lt
  not not_4 (Const_enable, priority_encoder_5_en_out);
  Priority_Encoder #(.select(1)) priority_encoder_5 (
    .in0(or_5_out), .in1(or_6_out), .out(priority_encoder_5_out), .en_out(priority_encoder_5_en_out));  // open: gs, en_in
  and and_23 (DIV, _000000, comparator_26_eq);
  and and_24 (MFHI, _000000, comparator_27_eq);
  Comparator #(.width(6), .mode("unsigned")) comparator_29 (
    .a({6{1'b1}}), .b(Func_code), .eq(comparator_29_eq));  // open: gt, lt
  Multiplexer #(.enable("false")) multiplexer_4 (
    .in0(priority_encoder_5_out), .in1(1'b0), .out(Const_op), .sel(priority_encoder_5_en_out));
  not not_5 (BRANCH, priority_encoder_6_en_out);
  Priority_Encoder #(.select(2)) priority_encoder_6 (
    .in1(or_7_out), .in2(J), .in3(JR), .out(priority_encoder_6_out), .en_out(priority_encoder_6_en_out));  // open: in0, gs, en_in
  and and_25 (HALT, _111111, comparator_29_eq);
  Multiplexer #(.width(2), .enable("false")) multiplexer_5 (
    .in0(priority_encoder_6_out), .in1(2'b00), .out(Branch_op), .sel(priority_encoder_6_en_out));
  Comparator #(.width(6), .mode("unsigned")) comparator_30 (.a(6'b001101), .b(Op_code), .eq(ORI));  // open: gt, lt
  Comparator #(.width(6), .mode("unsigned")) comparator_31 (
    .a(6'b011011), .b(Func_code), .eq(comparator_31_eq));  // open: gt, lt
  Comparator #(.width(6), .mode("unsigned")) comparator_32 (
    .a(6'b010010), .b(Func_code), .eq(comparator_32_eq));  // open: gt, lt
  Comparator #(.width(6), .mode("unsigned")) comparator_33 (.a(6'b000010), .b(Op_code), .eq(J));  // open: gt, lt
  Comparator #(.width(6), .mode("unsigned")) comparator_34 (
    .a(6'b000001), .b(Func_code), .eq(comparator_34_eq));  // open: gt, lt
  and and_26 (DIVU, _000000, comparator_31_eq);
  and and_27 (MFLO, _000000, comparator_32_eq);
  and and_28 (TTY, _111111, comparator_34_eq);
  or or_8 (HI_LO_write, MULT, MULU, DIV, DIVU);
  or or_9 (or_9_out, LW, POP);
  or or_10 (or_10_out, ADDI, ANDI, ORI, XORI, SLTI, SLTIU, LW);
  Priority_Encoder priority_encoder_7 (
    .in1(or_9_out), .in2(MFHI), .in3(MFLO), .in4(RND), .in5(KBD), .out(priority_encoder_7_out),
    .en_out(priority_encoder_7_en_out));  // open: in0, in6, in7, en_in, gs
  Multiplexer #(.width(5), .enable("false")) multiplexer_6 (.in0(Rd), .in1(Rt), .out(Write_address), .sel(or_10_out));
  Multiplexer #(.width(3), .enable("false")) multiplexer_7 (
    .in0(priority_encoder_7_out), .in1(3'b000), .out(Register_Select), .sel(priority_encoder_7_en_out));
  Comparator #(.width(6), .mode("unsigned")) comparator_35 (.a(6'b001000), .b(Op_code), .eq(ADDI));  // open: gt, lt
  Comparator #(.width(6), .mode("unsigned")) comparator_36 (.a(6'b001110), .b(Op_code), .eq(XORI));  // open: gt, lt
  Comparator #(.width(6), .mode("unsigned")) comparator_37 (
    .a({6{1'b0}}), .b(Func_code), .eq(comparator_37_eq));  // open: gt, lt
  Comparator #(.width(6), .mode("unsigned")) comparator_38 (
    .a(6'b001000), .b(Func_code), .eq(comparator_38_eq));  // open: gt, lt
  and and_29 (JR, _000000, comparator_38_eq);
  Comparator #(.width(6), .mode("unsigned")) comparator_39 (
    .a(6'b000010), .b(Func_code), .eq(comparator_39_eq));  // open: gt, lt
  not not_6 (STACK, priority_encoder_8_en_out);
  Priority_Encoder #(.select(1)) priority_encoder_8 (
    .in0(POP), .in1(Ram_value_select), .out(priority_encoder_8_out), .en_out(priority_encoder_8_en_out));  // open: gs, en_in
  and and_30 (NOP, _000000, comparator_37_eq);
  and and_31 (RND, _111111, comparator_39_eq);
  Multiplexer #(.enable("false")) multiplexer_8 (
    .in0(priority_encoder_8_out), .in1(1'b0), .out(Sp_op), .sel(priority_encoder_8_en_out));
  or or_11 (or_11_out, LW, SW);
  Priority_Encoder #(.select(2)) priority_encoder_9 (
    .in1(or_11_out), .in2(STACK), .out(priority_encoder_9_out), .en_out(priority_encoder_9_en_out));  // open: in0, in3, gs, en_in
  Multiplexer #(.width(2), .enable("false")) multiplexer_9 (
    .in0(priority_encoder_9_out), .in1(2'b00), .out(Ram_address_select), .sel(priority_encoder_9_en_out));

  assign Stack_op = Sp_op;

  // Other names for the same wires on the sheet: ZERO_F = Flags[0]; SIGN_F = Flags[1]; FUNC[5:0] = Func_code;
  //   OP_t[5:0] = Op_code; PUSH = Ram_value_select

  // Notes on the sheet:
  //   AND
  //   KBD
  //   ADD
  //   SLT
  //   BEQ
  //   LW
  //   Control Unit op
  //   OR
  //   SUB
  //   SLTU
  //   BNE
  //   SW
  //   MULT
  //   NOR
  //   SLTI
  //   BLEZ
  //   POP
  //   ALU Control
  //   MULU
  //   XOR
  //   SLTIU
  //   BGTZ
  //   PUSH
  //   Constant Unit Control
  //   Branch Control
  //   DIV
  //   ANDI
  //   MFHI
  //   BLTZ
  //   HALT
  //   DIVU
  //   ORI
  //   MFLO
  //   J
  //   TTY
  //   Register File Control
  //   NOP
  //   JR
  //   ADDI
  //   XORI
  //   RND
  //   Ram Control
endmodule
