// Logisim project Datapath.circ as structural Verilog: 10 circuits, main circuit main
module main (
  input  [4:0] Register_read_address_1,
  input  [4:0] Register_read_address_2,
  input  Hi_Lo_register_read_address,
  input  Hi_Lo_value_enable,
  input  [31:0] Immediate_value,
  input  Immediate_value_enable,
  input  [15:0] Const,
  input  Const_enable,
  input  [4:0] Register_write_address,
  input  Constant_unit_operation,
  input  [2:0] Alu_operation_code,
  input  [1:0] Mult_Div_operation_code,
  input  [1:0] Pc_operation_code,
  input  [1:0] Sp_operation_code,
  input  Register_write,
  input  Mult_div_write,
  input  [25:0] Jump,
  input  [1:0] Target_address,
  input  Data_write,
  input  RND,
  input  KBD,
  input  KBD_AV,
  input  [6:0] KBD_D,
  input  Busy_sign,
  input  Reset,
  input  Clock,
  output [31:0] Ram_address,
  output [31:0] Data_write_2,
  output [1:0] Flags,
  output [6:0] out_30
);

  wire and_1_out, and_3_out, and_4_out, not_1_out, not_2_out, not_3_out, not_4_out, not_5_out;
  wire [1:0] bit_extender_2_out, bit_extender_3_out, or_1_out;
  wire [1:1] and_2_out;
  wire [27:0] PC_VALUE;
  wire [29:0] bit_extender_4_out;
  wire [30:0] ALU_RESULT;
  wire [31:0] bit_extender_1_out, BRANCH_TARGET, CONST_EXT, HI_READ, HI_RESULT, LO_READ, LO_RESULT,
       multiplexer_1_out, multiplexer_2_out, multiplexer_3_out, multiplexer_4_out, multiplexer_5_out,
       multiplexer_6_out, PC_PLUS_4, random_1_out, RRD2, SELECT_VALUE, SP_MINUS_4, SP_PLUS_4, SP_VALUE;
  wire [31:7] RRD1;
  wire [31:28] JUMP_V;

  Multiplexer #(.width(32), .enable("false")) multiplexer_1 (
    .in0({Flags[1], ALU_RESULT}), .in1(Immediate_value), .out(multiplexer_1_out), .sel(Immediate_value_enable));
  Random #(.width(32)) random_1 (.clk(Clock), .out(random_1_out));  // open: next, clr
  Multiplexer #(.width(32), .enable("false")) multiplexer_2 (
    .in0(multiplexer_1_out), .in1(random_1_out), .out(multiplexer_2_out), .sel(RND));
  assign bit_extender_1_out = {{25{1'b0}}, KBD_D};  // Bit_Extender bit_extender_1
  Multiplexer #(.width(32), .enable("false")) multiplexer_3 (
    .in0({32{1'b1}}), .in1(bit_extender_1_out), .out(multiplexer_3_out), .sel(KBD_AV));
  not not_1 (not_1_out, Hi_Lo_register_read_address);
  and and_1 (and_1_out, not_1_out, Hi_Lo_value_enable);
  and and_2 (and_2_out[1], Hi_Lo_value_enable, Hi_Lo_register_read_address);
  Multiplexer #(.width(32), .enable("false")) multiplexer_4 (
    .in0(multiplexer_2_out), .in1(multiplexer_3_out), .out(multiplexer_4_out), .sel(KBD));
  assign bit_extender_2_out = {{1{1'b0}}, and_1_out};  // Bit_Extender bit_extender_2
  assign bit_extender_3_out = {{1{Const_enable}}, Const_enable};  // Bit_Extender bit_extender_3
  not not_2 (not_2_out, Busy_sign);
  Multiplexer #(.select(2), .width(32), .enable("false")) multiplexer_5 (
    .in0(PC_PLUS_4), .in1(BRANCH_TARGET), .in2({JUMP_V, Jump, 2'b00}), .in3({Flags[1], ALU_RESULT}),
    .out(multiplexer_5_out), .sel(Pc_operation_code));
  not not_3 (not_3_out, Busy_sign);
  and and_3 (and_3_out, Mult_div_write, not_2_out);
  Multiplexer #(.select(2), .width(32), .enable("false")) multiplexer_6 (
    .in0(SP_VALUE), .in1(SP_PLUS_4), .in2(SP_MINUS_4), .out(multiplexer_6_out), .sel(Sp_operation_code));  // open: in3
  Multiplexer #(.select(2), .width(32), .enable("false")) multiplexer_7 (
    .in0(RRD2), .in1(HI_READ), .in2(LO_READ), .in3(CONST_EXT), .out(SELECT_VALUE), .sel(or_1_out));
  assign or_1_out = bit_extender_2_out | {and_2_out[1], 1'b0} | bit_extender_3_out;  // OR_Gate or_1, 2 bits wide
  and and_4 (and_4_out, Register_write, not_3_out);
  not not_4 (not_4_out, Busy_sign);
  not not_5 (not_5_out, Busy_sign);
  hi_lo_register hi_lo_register_1 (
    .number_hight(HI_RESULT), .low_number(LO_RESULT), .Register_write_enable(and_3_out), .clock(Clock),
    .hight_result(HI_READ), .Low_result(LO_READ), .Reset(Reset));
  Register #(.width(32)) PC (.D(multiplexer_5_out), .en(not_4_out), .Q({JUMP_V, PC_VALUE}), .clk(Clock), .clr(Reset));
  Register #(.width(32)) SP (.D(multiplexer_6_out), .en(not_5_out), .Q(SP_VALUE), .clk(Clock), .clr(Reset));
  register_file register_file_1 (
    .Register_read_address_1(Register_read_address_1), .Register_read_address_2(Register_read_address_2),
    .Register_write_address(Register_write_address), .Data_write(multiplexer_4_out),
    .Register_write_enable(and_4_out), .Reset(Reset), .Clock(Clock), .Register_read_data_1({RRD1, out_30}),
    .Register_read_data_2(RRD2));
  assign bit_extender_4_out = {{14{Const[15]}}, Const};  // Bit_Extender bit_extender_4
  Adder #(.width(32)) adder_1 (.a(SP_VALUE), .b(32'h4), .out(SP_PLUS_4));  // open: cin, cout
  Subtractor #(.width(32)) subtractor_1 (.a(SP_VALUE), .b(32'h4), .out(SP_MINUS_4));  // open: bin, bout
  constant_unit constant_unit_1 (.in_1(Const), .in_2(Constant_unit_operation), .Const_ext(CONST_EXT));
  Comparator #(.width(32)) comparator_1 (.a({Flags[1], ALU_RESULT}), .b({32{1'b0}}), .eq(Flags[0]));  // open: gt, lt
  alu alu_1 (
    .Number_a({RRD1, out_30}), .Number_b(SELECT_VALUE), .Operation_code(Alu_operation_code),
    .Result({Flags[1], ALU_RESULT}));
  Adder #(.width(32)) adder_2 (.a({JUMP_V, PC_VALUE}), .b(32'h4), .out(PC_PLUS_4));  // open: cin, cout
  Adder #(.width(32)) adder_3 (.a(PC_PLUS_4), .b({bit_extender_4_out, 2'b00}), .out(BRANCH_TARGET));  // open: cin, cout
  multiply_divide_unit multiply_divide_unit_1 (
    .Number_a({RRD1, out_30}), .Number_b(SELECT_VALUE), .Operation_code(Mult_Div_operation_code),
    .hight(HI_RESULT), .Low(LO_RESULT));
  Multiplexer #(.width(32), .enable("false")) multiplexer_8 (
    .in0(RRD2), .in1({RRD1, out_30}), .out(Data_write_2), .sel(Data_write));
  Multiplexer #(.select(2), .width(32), .enable("false")) multiplexer_9 (
    .in0({JUMP_V, PC_VALUE}), .in1({Flags[1], ALU_RESULT}), .in2(SP_VALUE), .out(Ram_address),
    .sel(Target_address));  // open: in3

  // Other names for the same wires on the sheet: ALU_OP[2:0] = Alu_operation_code; BUSY = Busy_sign;
  //   CONST_ENB = Const_enable; CONST_OP = Constant_unit_operation; DATA_W = Data_write; ZERO_F = Flags[0];
  //   ALU_RESULT[31] = Flags[1]; SIGN_F = Flags[1]; HILO_ENB = Hi_Lo_value_enable;
  //   HILO_R = Hi_Lo_register_read_address; IMM_ENB = Immediate_value_enable; IMM_V[31:0] = Immediate_value;
  //   JUMP_V[27:2] = Jump; PC_VALUE[31:28] = JUMP_V; M_D_W = Mult_div_write;
  //   MULT_DIV_OP[1:0] = Mult_Div_operation_code; PC_OP[1:0] = Pc_operation_code; R_W = Register_write;
  //   RAM_A[31:0] = Ram_address; RR1[4:0] = Register_read_address_1; RR2[4:0] = Register_read_address_2;
  //   RRD1[6:0] = out_30; RW[4:0] = Register_write_address; SP_OP[1:0] = Sp_operation_code;
  //   TARGET_A[1:0] = Target_address
endmodule

module register_file (
  input  [4:0] Register_read_address_1,
  input  [4:0] Register_read_address_2,
  input  [4:0] Register_write_address,
  input  [31:0] Data_write,
  input  Register_write_enable,
  input  Reset,
  input  Clock,
  output [31:0] Register_read_data_1,
  output [31:0] Register_read_data_2
);

  wire W0, W1, W2, W3, W4, W5, W6, W7, W8, W9, W10, W11, W12, W13, W14, W15, W16, W17, W18, W19, W20, W21,
       W22, W23, W24, W25, W26, W27, W28, W29, W30;
  wire [31:0] R0, R1, R2, R3, R4, R5, R6, R7, R8, R9, R10, R11, R12, R13, R14, R15, R16, R17, R18, R19, R20,
       R21, R22, R23, R24, R25, R26, R27, R28, R29, R30, undriven, undriven_2, W_DATA;

  Register #(.width(32)) u_R0 (.D({32{1'b0}}), .en(W0), .Q(R0), .clk(Clock), .clr(Reset));
  Register #(.width(32)) u_R8 (.D(W_DATA), .en(W8), .Q(R8), .clk(Clock), .clr(Reset));
  Register #(.width(32)) u_R16 (.D(W_DATA), .en(W16), .Q(R16), .clk(Clock), .clr(Reset));
  Register #(.width(32)) u_R24 (.D(W_DATA), .en(W24), .Q(R24), .clk(Clock), .clr(Reset));
  Register #(.width(32)) u_R1 (.D(W_DATA), .en(W1), .Q(R1), .clk(Clock), .clr(Reset));
  Register #(.width(32)) u_R9 (.D(W_DATA), .en(W9), .Q(R9), .clk(Clock), .clr(Reset));
  Register #(.width(32)) u_R17 (.D(W_DATA), .en(W17), .Q(R17), .clk(Clock), .clr(Reset));
  Register #(.width(32)) u_R25 (.D(W_DATA), .en(W25), .Q(R25), .clk(Clock), .clr(Reset));
  Decoder #(.select(5)) decoder_1 (
    .out0(W0), .out1(W1), .out2(W2), .out3(W3), .out4(W4), .out5(W5), .out6(W6), .out7(W7), .out8(W8),
    .out9(W9), .out10(W10), .out11(W11), .out12(W12), .out13(W13), .out14(W14), .out15(W15), .out16(W16),
    .out17(W17), .out18(W18), .out19(W19), .out20(W20), .out21(W21), .out22(W22), .out23(W23), .out24(W24),
    .out25(W25), .out26(W26), .out27(W27), .out28(W28), .out29(W29), .out30(W30),
    .sel(Register_write_address), .en(Register_write_enable));  // open: out31
  Register #(.width(32)) u_R2 (.D(W_DATA), .en(W2), .Q(R2), .clk(Clock), .clr(Reset));
  Register #(.width(32)) u_R10 (.D(W_DATA), .en(W10), .Q(R10), .clk(Clock), .clr(Reset));
  Register #(.width(32)) u_R18 (.D(W_DATA), .en(W18), .Q(R18), .clk(Clock), .clr(Reset));
  Register #(.width(32)) u_R26 (.D(W_DATA), .en(W26), .Q(R26), .clk(Clock), .clr(Reset));
  Register #(.width(32)) u_R3 (.D(W_DATA), .en(W3), .Q(R3), .clk(Clock), .clr(Reset));
  Register #(.width(32)) u_R11 (.D(W_DATA), .en(W11), .Q(R11), .clk(Clock), .clr(Reset));
  Register #(.width(32)) u_R19 (.D(W_DATA), .en(W19), .Q(R19), .clk(Clock), .clr(Reset));
  Register #(.width(32)) u_R27 (.D(W_DATA), .en(W27), .Q(R27), .clk(Clock), .clr(Reset));
  Register #(.width(32)) u_R4 (.D(W_DATA), .en(W4), .Q(R4), .clk(Clock), .clr(Reset));
  Register #(.width(32)) u_R12 (.D(W_DATA), .en(W12), .Q(R12), .clk(Clock), .clr(Reset));
  Register #(.width(32)) u_R20 (.D(W_DATA), .en(W20), .Q(R20), .clk(Clock), .clr(Reset));
  Register #(.width(32)) u_R28 (.D(W_DATA), .en(W28), .Q(R28), .clk(Clock), .clr(Reset));
  Multiplexer #(.select(5), .width(32), .enable("false")) multiplexer_1 (
    .in0(R0), .in1(R1), .in2(R2), .in3(R3), .in4(R4), .in5(R5), .in6(R6), .in7(R7), .in8(R8), .in9(R9),
    .in10(R10), .in11(R11), .in12(R12), .in13(R13), .in14(R14), .in15(R15), .in16(R16), .in17(R17),
    .in18(R18), .in19(R19), .in20(R20), .in21(R21), .in22(R22), .in23(R23), .in24(R24), .in25(R25),
    .in26(R26), .in27(R27), .in28(R28), .in29(R29), .in30(R30), .in31(undriven), .out(Register_read_data_1),
    .sel(Register_read_address_1));
  Register #(.width(32)) u_R5 (.D(W_DATA), .en(W5), .Q(R5), .clk(Clock), .clr(Reset));
  Register #(.width(32)) u_R13 (.D(W_DATA), .en(W13), .Q(R13), .clk(Clock), .clr(Reset));
  Register #(.width(32)) u_R21 (.D(W_DATA), .en(W21), .Q(R21), .clk(Clock), .clr(Reset));
  Register #(.width(32)) u_R29 (.D(W_DATA), .en(W29), .Q(R29), .clk(Clock), .clr(Reset));
  Register #(.width(32)) u_R6 (.D(W_DATA), .en(W6), .Q(R6), .clk(Clock), .clr(Reset));
  Register #(.width(32)) u_R14 (.D(W_DATA), .en(W14), .Q(R14), .clk(Clock), .clr(Reset));
  Register #(.width(32)) u_R22 (.D(W_DATA), .en(W22), .Q(R6), .clk(Clock), .clr(Reset));
  Register #(.width(32)) u_R30 (.D(W_DATA), .en(W30), .Q(R30), .clk(Clock), .clr(Reset));
  Register #(.width(32)) u_R7 (.D(W_DATA), .en(W7), .Q(R7), .clk(Clock), .clr(Reset));
  Register #(.width(32)) u_R15 (.D(W_DATA), .en(W15), .Q(R15), .clk(Clock), .clr(Reset));
  Register #(.width(32)) u_R23 (.D(W_DATA), .en(W23), .Q(R23), .clk(Clock), .clr(Reset));
  Multiplexer #(.select(5), .width(32), .enable("false")) multiplexer_2 (
    .in0(R0), .in1(R1), .in2(R2), .in3(R3), .in4(R4), .in5(R5), .in6(R6), .in7(R7), .in8(R8), .in9(R9),
    .in10(R10), .in11(R11), .in12(R12), .in13(R13), .in14(R14), .in15(R15), .in16(R16), .in17(R17),
    .in18(R18), .in19(R19), .in20(R20), .in21(R21), .in22(R22), .in23(R23), .in24(R24), .in25(R25),
    .in26(R26), .in27(R27), .in28(R28), .in29(R29), .in30(R30), .in31(undriven_2),
    .out(Register_read_data_2), .sel(Register_read_address_2));

  // Other names for the same wires on the sheet: DW[31:0] = Data_write; RR1[4:0] = Register_read_address_1;
  //   RR2[4:0] = Register_read_address_2; RW[4:0] = Register_write_address; RWE = Register_write_enable
endmodule

module alu (
  input  [31:0] Number_a,
  input  [31:0] Number_b,
  input  [2:0] Operation_code,
  output [31:0] Result
);

  wire [0:0] SLT, SLTU;
  wire [31:0] ADD, AND, not_1_out, OR, SUB, XOR;

  Adder #(.width(32)) adder_1 (.a(Number_a), .b(Number_b), .out(ADD));  // open: cin, cout
  Subtractor #(.width(32)) subtractor_1 (.a(Number_a), .b(Number_b), .out(SUB));  // open: bin, bout
  assign AND = Number_a & Number_b;  // AND_Gate and_1, 32 bits wide
  assign OR = Number_a | Number_b;  // OR_Gate or_1, 32 bits wide
  assign XOR = Number_a ^ Number_b;  // XOR_Gate xor_1, 32 bits wide
  Multiplexer #(.select(3), .width(32), .enable("false")) multiplexer_1 (
    .in0(ADD), .in1(SUB), .in2(AND), .in3(OR), .in4(not_1_out), .in5(XOR), .in6({{31{1'b0}}, SLT[0]}),
    .in7({{31{1'b0}}, SLTU[0]}), .out(Result), .sel(Operation_code));
  assign not_1_out = ~OR;  // NOT_Gate not_1, 32 bits wide
  Comparator #(.width(32)) comparator_1 (.a(Number_a), .b(Number_b), .lt(SLT[0]));  // open: gt, eq
  Comparator #(.width(32), .mode("unsigned")) comparator_2 (.a(Number_a), .b(Number_b), .lt(SLTU[0]));  // open: gt, eq

  // Other names for the same wires on the sheet: OP[2:0] = Operation_code; RS[31:0] = Number_a; RT[31:0] = Number_b

  // Notes on the sheet:
  //   ADD
  //   SUB
  //   AND
  //   OR
  //   XOR
  //   SLT
  //   SLTU
endmodule

module multiply_divide_unit (
  input  [31:0] Number_a,
  input  [31:0] Number_b,
  input  [1:0] Operation_code,
  output [31:0] hight,
  output [31:0] Low
);

  wire [31:0] DIV_HI, DIV_LO, DIVU_HI, DIVU_LO, MULT_HI, MULT_LO, MULU_HI, MULU_LO;

  mult_op mult_op_1 (.Number_a(Number_a), .Number_b(Number_b), .Low_result(MULT_LO), .Hight_result(MULT_HI));
  Multiplier #(.width(32)) multiplier_1 (.a(Number_a), .b(Number_b), .out(MULU_LO), .cout(MULU_HI));  // open: cin
  Multiplexer #(.select(2), .width(32), .enable("false")) multiplexer_1 (
    .in0(MULT_LO), .in1(MULU_LO), .in2(DIV_LO), .in3(DIVU_LO), .out(Low), .sel(Operation_code));
  Multiplexer #(.select(2), .width(32), .enable("false")) multiplexer_2 (
    .in0(MULT_HI), .in1(MULU_HI), .in2(DIV_HI), .in3(DIVU_HI), .out(hight), .sel(Operation_code));
  div_op div_op_1 (.Number_a(Number_a), .Number_b(Number_b), .Low(DIV_LO), .Hight(DIV_HI));
  Divider #(.width(32)) divider_1 (.a(Number_a), .b(Number_b), .out(DIVU_LO), .rem(DIVU_HI));  // open: upper

  // Other names for the same wires on the sheet: OP[1:0] = Operation_code; RS[31:0] = Number_a; RT[31:0] = Number_b

  // Notes on the sheet:
  //   MULT
  //   MULU
  //   DIV
  //   DIVU
endmodule

module mult_op (
  input  [31:0] Number_a,
  input  [31:0] Number_b,
  output [31:0] Low_result,
  output [31:0] Hight_result
);

  wire adder_1_cout, SIGN;
  wire [31:0] absolute_value_1_absolute_value, absolute_value_2_absolute_value, adder_1_out, adder_2_out,
       bit_extender_1_out, multiplier_1_cout, multiplier_1_out, not_1_out, not_2_out;

  xor xor_1 (SIGN, Number_a[31], Number_b[31]);
  absolute_value absolute_value_1 (.Number(Number_a), .Absolute_value(absolute_value_1_absolute_value));
  absolute_value absolute_value_2 (.Number(Number_b), .Absolute_value(absolute_value_2_absolute_value));
  Multiplier #(.width(32)) multiplier_1 (
    .a(absolute_value_1_absolute_value), .b(absolute_value_2_absolute_value), .out(multiplier_1_out),
    .cout(multiplier_1_cout));  // open: cin
  assign not_1_out = ~multiplier_1_out;  // NOT_Gate not_1, 32 bits wide
  assign not_2_out = ~multiplier_1_cout;  // NOT_Gate not_2, 32 bits wide
  Adder #(.width(32)) adder_1 (.a(not_1_out), .b(32'h1), .out(adder_1_out), .cout(adder_1_cout));  // open: cin
  assign bit_extender_1_out = {{31{1'b0}}, adder_1_cout};  // Bit_Extender bit_extender_1
  Adder #(.width(32)) adder_2 (.a(bit_extender_1_out), .b(not_2_out), .out(adder_2_out));  // open: cin, cout
  Multiplexer #(.width(32), .enable("false")) multiplexer_1 (
    .in0(multiplier_1_cout), .in1(adder_2_out), .out(Hight_result), .sel(SIGN));
  Multiplexer #(.width(32), .enable("false")) multiplexer_2 (
    .in0(multiplier_1_out), .in1(adder_1_out), .out(Low_result), .sel(SIGN));

  // Other names for the same wires on the sheet: RS[31:0] = Number_a; RT[31:0] = Number_b
endmodule

module absolute_value (
  input  [31:0] Number,
  output [31:0] Absolute_value
);

  wire [31:0] two_s_complement_1_complement;

  two_s_complement two_s_complement_1 (.Number(Number), .Complement(two_s_complement_1_complement));
  Multiplexer #(.width(32), .enable("false")) multiplexer_1 (
    .in0(Number), .in1(two_s_complement_1_complement), .out(Absolute_value), .sel(Number[31]));
endmodule

module two_s_complement (
  input  [31:0] Number,
  output [31:0] Complement
);

  wire [31:0] not_1_out;

  assign not_1_out = ~Number;  // NOT_Gate not_1, 32 bits wide
  Adder #(.width(32)) adder_1 (.a(not_1_out), .b(32'h1), .out(Complement));  // open: cin, cout
endmodule

module div_op (
  input  [31:0] Number_a,
  input  [31:0] Number_b,
  output [31:0] Low,
  output [31:0] Hight
);

  wire SIGN;
  wire [31:0] absolute_value_1_absolute_value, absolute_value_2_absolute_value, divider_1_out, divider_1_rem,
       two_s_complement_1_complement, two_s_complement_2_complement;

  xor xor_1 (SIGN, Number_a[31], Number_b[31]);
  absolute_value absolute_value_1 (.Number(Number_a), .Absolute_value(absolute_value_1_absolute_value));
  absolute_value absolute_value_2 (.Number(Number_b), .Absolute_value(absolute_value_2_absolute_value));
  Divider #(.width(32)) divider_1 (
    .a(absolute_value_1_absolute_value), .b(absolute_value_2_absolute_value), .out(divider_1_out),
    .rem(divider_1_rem));  // open: upper
  two_s_complement two_s_complement_1 (.Number(divider_1_out), .Complement(two_s_complement_1_complement));
  two_s_complement two_s_complement_2 (.Number(divider_1_rem), .Complement(two_s_complement_2_complement));
  Multiplexer #(.width(32), .enable("false")) multiplexer_1 (
    .in0(divider_1_out), .in1(two_s_complement_1_complement), .out(Low), .sel(SIGN));
  Multiplexer #(.width(32), .enable("false")) multiplexer_2 (
    .in0(divider_1_rem), .in1(two_s_complement_2_complement), .out(Hight), .sel(Number_a[31]));

  // Other names for the same wires on the sheet: RS[31:0] = Number_a; RT[31:0] = Number_b
endmodule

module hi_lo_register (
  input  [31:0] number_hight,
  input  [31:0] low_number,
  input  Register_write_enable,
  input  Reset,
  input  clock,
  output [31:0] hight_result,
  output [31:0] Low_result
);

  wire W;

  Register #(.width(32)) HI (.D(number_hight), .en(W), .Q(hight_result), .clk(clock), .clr(Reset));
  Register #(.width(32)) LO (.D(low_number), .en(W), .Q(Low_result), .clk(clock), .clr(Reset));

  // Other names for the same wires on the sheet: W_HI[31:0] = number_hight; W_LO[31:0] = low_number;
  //   Write = Register_write_enable
endmodule

module constant_unit (
  input  [15:0] in_1,
  input  in_2,
  output [31:0] Const_ext
);

  wire [31:0] bit_extender_1_out, bit_extender_2_out;

  assign bit_extender_1_out = {{16{in_1[15]}}, in_1};  // Bit_Extender bit_extender_1
  assign bit_extender_2_out = {{16{1'b0}}, in_1};  // Bit_Extender bit_extender_2
  Multiplexer #(.width(32), .enable("false")) multiplexer_1 (
    .in0(bit_extender_1_out), .in1(bit_extender_2_out), .out(Const_ext), .sel(in_2));

  // Other names for the same wires on the sheet: CONST[15:0] = in_1; OP = in_2
endmodule
