// Logisim project Memory Interface.circ as structural Verilog: 1 circuit, main circuit main
module main (
  input  [31:0] Target_Address,
  input  [31:0] Ram_O0,
  input  [31:0] Ram_O1,
  input  [31:0] To_Write,
  input  [31:0] Ram_O2,
  input  [31:0] Ram_O3,
  output [15:0] Address,
  output [3:0] Mask,
  output [31:0] Ram_I0,
  output [31:0] Ram_I1,
  output [31:0] Ram_out,
  output [31:0] Ram_I2,
  output [31:0] Ram_I3
);

  wire [31:0] divider_1_out;
  wire [31:16] divider_2_out;

  Multiplexer #(.select(2), .width(32), .enable("false")) multiplexer_1 (
    .in0(Ram_O0), .in1(Ram_O1), .in2(Ram_O2), .in3(Ram_O3),
    .out({Ram_out[7:0], Ram_out[15:8], Ram_out[23:16], Ram_out[31:24]}), .sel(divider_1_out[1:0]));
  Divider #(.width(32)) divider_1 (.a(Target_Address), .b(32'h4), .out(divider_1_out));  // open: upper, rem
  Decoder #(.select(2), .enable("false")) decoder_1 (
    .out0(Mask[0]), .out1(Mask[1]), .out2(Mask[2]), .out3(Mask[3]), .sel(divider_1_out[1:0]));
  Divider #(.width(32)) divider_2 (.a(divider_1_out), .b(32'h4), .out({divider_2_out, Address}));  // open: upper, rem

  assign Ram_I0 = {To_Write[7:0], To_Write[15:8], To_Write[23:16], To_Write[31:24]};
  assign Ram_I1 = {To_Write[7:0], To_Write[15:8], To_Write[23:16], To_Write[31:24]};
  assign Ram_I2 = {To_Write[7:0], To_Write[15:8], To_Write[23:16], To_Write[31:24]};
  assign Ram_I3 = {To_Write[7:0], To_Write[15:8], To_Write[23:16], To_Write[31:24]};
endmodule
